# Fritzing sketch arduino-isp (saved by Fritzing 0.9.2b)
breadboards: 1

parts:
  ATmega328 = atmega328 [package=dip]
  LED = LED - 5mm [color="Red (633nm)" package="5 mm [THT]"]
  R1 = Resistor [tolerance=±5% resistance=220 package=THT]
  Part1 = Arduino Uno (Rev3) - ICSP

nets:
  N1: ATmega328.RESET, Part1.D10_PWM/SS
  VCC: ATmega328.VCC, ATmega328.AVCC, Part1.5V
  GND: ATmega328.GND, LED.cathode, Part1.GND
  N2: ATmega328.D11_(PWM), Part1.D11_PWM/MOSI
  N3: ATmega328.D12, Part1.D12/MISO
  N4: ATmega328.D13, Part1.D13/SCK
  N5: ATmega328.A5, R1.Pin_0
  N6: LED.anode, R1.Pin_1
