# Fritzing sketch schematic (saved by Fritzing 0.9.2b)
breadboards: 1

parts:
  ATmega328 = atmega328 [package=dip]
  +5V = Power plug
  LED = LED - 5mm [color="Red (633nm)" package="5 mm [THT]"]
  R1 = Resistor [tolerance=±5% resistance=220 package=THT]

nets:
  VCC: ATmega328.VCC, ATmega328.AVCC, +5V.VCC
  GND: ATmega328.GND, +5V.GND, LED.cathode
  N1: ATmega328.A5, R1.Pin_0
  N2: LED.anode, R1.Pin_1
